# Fritzing sketch diagram (saved by Fritzing 0.9.3b)
breadboards: 1

parts:
  Raspberry_Pi1 = Raspberry Pi 2
  R1 = Resistor [tolerance=±5% resistance=330 package=THT]  # not connected
  S3 = Pushbutton [package="[THT]"]  # not connected
  LED1 = LED - 3mm [color="Red (633nm)" package="3 mm [THT]"]

nets:
  N1: Raspberry_Pi1.GND, LED1.cathode

notes:
  BUSY
  RST
  DC
  CS
  CLK
  DIN
  GND
  3v3
